# Fritzing sketch FSR (saved by Fritzing 0.9.3b)
breadboards: 1

parts:
  J1 = Basic Force Sensing Resistor (FSR) [package=THT]
  Part1 = Arduino Uno (Rev3) - ICSP
  R1 = Trimmer Potentiometer [maximum_resistance=10kΩ package=THT]
  Part2 = MicroSD Card Module  # not connected
  VCC1 = Battery

nets:
  N1: J1.pin_0, Part1.A0, R1.wiper
  N2: J1.pin_1, Part1.5V
  N3: Part1.GND, R1.leg1, VCC1.-
  N4: Part1.VIN, VCC1.+

notes:
  Vcc - 5V
  Gnd - Gnd
  MOSI - pin 11
  MISO - pin 12
  CLK - pin 13
  CS - pin 4
